# Fritzing sketch pxt-servo (saved by Fritzing 0.9.3b)

parts:
  R1 = BBC MicroBit
  PWM1 = PCA9685 16x12-bit PWM Breakout
  J2 = Basic Servo
  VCC1 = 4 x AAA Battery Mount

nets:
  GND: R1.GND, PWM1.no_name_yet#501, PWM1.no_name_yet#701, PWM1.no_name_yet#1000, J2.gnd, VCC1.-
  N1: R1.P20_(SDA), PWM1.no_name_yet#504
  N2: R1.P19_(SCL), PWM1.no_name_yet#503
  N3: R1.3v3, PWM1.no_name_yet#505
  N4: PWM1.no_name_yet#0, J2.pulse
  N5: PWM1.no_name_yet#100, PWM1.no_name_yet#706, J2.vcc, VCC1.+

custom parts:
  BBC MicroBit: The BBC MICRO:BIT
